# Fritzing sketch progetto_1 (saved by Fritzing 0.9.3b)
breadboards: 1

parts:
  Part1 = Arduino Uno (Rev3)
  S1 = Pushbutton [package="[THT]"]
  S2 = Pushbutton [package="[THT]"]
  S3 = Pushbutton [package="[THT]"]
  LED2 = smd LED [color="Green (570nm)" package="1206 [SMD]"]
  LED3 = smd LED [color="Green (570nm)" package="1206 [SMD]"]
  LED4 = smd LED [color="Green (570nm)" package="1206 [SMD]"]
  R1 = Resistor [tolerance=±5% resistance=220 package=THT]
  R2 = Resistor [tolerance=±5% resistance=220 package=THT]
  R3 = Resistor [tolerance=±5% resistance=220 package=THT]
  R4 = Resistor [tolerance=±5% resistance=220 package=THT]
  R5 = Resistor [tolerance=±5% resistance=10k package=THT]
  R6 = Resistor [tolerance=±5% resistance=10k package=THT]
  R7 = Resistor [tolerance=±5% resistance=10k package=THT]
  R8 = Rotary Potentiometer (Small) [maximum_resistance=100kΩ package=THT]
  LED5 = LED - 5mm [color="Red (633nm)" package="5 mm [THT]"]

nets:
  N1: Part1.A0, R8.wiper
  N2: Part1.D10_PWM/SS, R3.Pin_1
  N3: Part1.D11_PWM/MOSI, R1.Pin_1
  N4: Part1.D12/MISO, R2.Pin_1
  N5: Part1.D2, S3.Pin_3, S3.Pin_4, R6.Pin_0
  N6: Part1.D3_PWM, S2.Pin_3, S2.Pin_4, R7.Pin_0
  N7: Part1.D5_PWM, R4.Pin_1
  N8: Part1.D7, S1.Pin_3, S1.Pin_4, R5.Pin_0
  N9: Part1.5V, S1.Pin_1, S1.Pin_2, S2.Pin_1, S2.Pin_2, S3.Pin_1, S3.Pin_2, R8.leg2
  N10: Part1.GND, LED2.cathode, LED3.cathode, LED4.cathode, R5.Pin_1, R6.Pin_1, R7.Pin_1, R8.leg1, LED5.cathode
  N11: LED2.anode, R1.Pin_0
  N12: LED3.anode, R2.Pin_0
  N13: LED4.anode, R3.Pin_0
  N14: R4.Pin_0, LED5.anode
