# Fritzing sketch smart_cm (saved by Fritzing 0.9.3b)
breadboards: 1

parts:
  Part1 = Arduino Uno (Rev3)
  hc-sr1 = hc-sr04
  PIR1 = PIR sensor
  S1 = Pushbutton [package="[THT]"]
  R1 = Rotary Potentiometer (Small) [maximum_resistance=100kΩ package=THT]
  LED1 = LED - 5mm [color="Yellow (595nm)" package="5 mm [THT]"]
  LED2 = LED - 5mm [color="Yellow (595nm)" package="5 mm [THT]"]
  LED3 = LED - 5mm [color="Green (570nm)" package="5 mm [THT]"]
  R2 = Resistor [tolerance=±5% resistance=220 package=THT]
  R3 = Resistor [tolerance=±5% resistance=220 package=THT]
  R4 = Resistor [tolerance=±5% resistance=220 package=THT]
  R5 = Resistor [tolerance=±5% resistance=10k package=THT]

nets:
  N1: Part1.A0, R1.wiper
  N2: Part1.D8, hc-sr1.Echo
  N3: Part1.D9_PWM, S1.Pin_3, S1.Pin_4, R5.Pin_0
  N4: Part1.D3_PWM, R2.Pin_1
  N5: Part1.D4, R3.Pin_1
  N6: Part1.D5_PWM, R4.Pin_1
  N7: Part1.D6_PWM, PIR1.SIG
  N8: Part1.D7, hc-sr1.Trig
  5V: Part1.5V, hc-sr1.VCC, PIR1.VDD, S1.Pin_1, S1.Pin_2, R1.leg2
  GND: Part1.GND, hc-sr1.GND, PIR1.GND, R1.leg1, LED1.cathode, LED2.cathode, LED3.cathode, R5.Pin_1
  N9: LED1.anode, R2.Pin_0
  N10: LED2.anode, R3.Pin_0
  N11: LED3.anode, R4.Pin_0
